# Fritzing sketch Calculadora (saved by Fritzing 0.9.4)

parts:
  Componente3 = Arduino Mega 2560 (Rev3)
  Componente4 = LCD1602-I2C
  Generic_4x4_button_keypad1 = Generic 4x4 Keypad

nets:
  N1: Componente3.D21/SCL, Componente4.SCL
  N2: Componente3.D20/SDA, Componente4.SDA
  5V: Componente3.5V, Componente4.VCC
  GND: Componente3.GND, Componente4.GND
  N3: Componente3.D35, Generic_4x4_button_keypad1.C4
  N4: Componente3.D37, Generic_4x4_button_keypad1.C3
  N5: Componente3.D39, Generic_4x4_button_keypad1.C2
  N6: Componente3.D41, Generic_4x4_button_keypad1.C1
  N7: Componente3.D43, Generic_4x4_button_keypad1.R1
  N8: Componente3.D45, Generic_4x4_button_keypad1.R2
  N9: Componente3.D47, Generic_4x4_button_keypad1.R3
  N10: Componente3.D49, Generic_4x4_button_keypad1.R4

custom parts:
  LCD1602-I2C: A standard character display, usually with 2x16 characters. Comes in many colors with LCM1602 IIC attached.
  Generic 4x4 Keypad: generic 4x4 keypad 4 rows of four 6 mm tact switches cheap and nasty but works
