# Fritzing sketch DHT11LCDMega (saved by Fritzing 0.9.4)
breadboards: 1

parts:
  DHT1 = DHT11 Humitidy and Temperature Sensor
  Componente3 = Arduino Mega 2560 (Rev3)
  Componente4 = LCD1602-I2C

nets:
  VDD: DHT1.VDD, Componente3.5V, Componente4.VCC
  N1: DHT1.DATA, Componente3.D2_PWM
  GND: DHT1.GND, Componente3.GND, Componente4.GND
  N2: Componente3.D21/SCL, Componente4.SCL
  N3: Componente3.D20/SDA, Componente4.SDA

custom parts:
  DHT11 Humitidy and Temperature Sensor: DHT11 Humidity and Temperature Sensor
  LCD1602-I2C: A standard character display, usually with 2x16 characters. Comes in many colors with LCM1602 IIC attached.
