# Fritzing sketch DHT11Mega (saved by Fritzing 0.9.4)

parts:
  DHT1 = DHT11 Humitidy and Temperature Sensor
  Componente3 = Arduino Mega 2560 (Rev3)

nets:
  VDD: DHT1.VDD, Componente3.5V
  N1: DHT1.DATA, Componente3.D2_PWM
  GND: DHT1.GND, Componente3.GND

custom parts:
  DHT11 Humitidy and Temperature Sensor: DHT11 Humidity and Temperature Sensor
