# Fritzing sketch DHT11Uno (saved by Fritzing 0.9.4)

parts:
  Componente2 = Arduino Uno (Rev3)
  DHT1 = DHT11 Humitidy and Temperature Sensor

nets:
  N1: Componente2.D2, DHT1.DATA
  5V: Componente2.5V, DHT1.VDD
  GND: Componente2.GND, DHT1.GND

custom parts:
  DHT11 Humitidy and Temperature Sensor: DHT11 Humidity and Temperature Sensor
