# Fritzing sketch LedRGB2 (saved by Fritzing 0.9.4)
breadboards: 1

parts:
  Componente1 = Arduino Mega 2560 (Rev3)
  R1 = Resistor [tolerance=±5% resistance=220 package=THT]
  R2 = Resistor [tolerance=±5% resistance=220 package=THT]
  R3 = Resistor [tolerance=±5% resistance=220 package=THT]
  LED2 = RGB LED - (4 legs) [package="5 mm [THT]"]

nets:
  N1: Componente1.GND, LED2.common_anode
  N2: Componente1.D11_PWM, R3.Pin_0
  N3: Componente1.D10_PWM, R2.Pin_0
  N4: Componente1.D9_PWM, R1.Pin_0
  N5: R1.Pin_1, LED2.blue_cathode
  N6: R2.Pin_1, LED2.green_cathode
  N7: R3.Pin_1, LED2.red_cathode
