# Fritzing sketch LedRGBJoystick (saved by Fritzing 0.9.4)

parts:
  Part1 = KY-009 Full Color RGB LED SMD Module [package="Breakout board"]
  Componente1 = Arduino Mega 2560 (Rev3)
  Componente2 = Thumb Joystick

nets:
  GND: Part1.-, Componente1.GND, Componente2.GND
  N1: Part1.R, Componente1.D9_PWM
  N2: Part1.G, Componente1.D10_PWM
  N3: Part1.B, Componente1.D11_PWM
  N4: Componente1.A0, Componente2.VERT
  N5: Componente1.A1, Componente2.HORZ
  N6: Componente1.A2, Componente2.SEL
  5V: Componente1.5V, Componente2.VCC

custom parts:
  KY-009 Full Color RGB LED SMD Module: RGB full color LED Module KY-009 for Arduino, emits a range of colors by mixing red, green and blue. The amount of each primary color is adjusted using PWM.
