# Fritzing sketch Meteo (saved by Fritzing 0.9.4)
breadboards: 1

parts:
  Componente1 = Arduino Uno (Rev3)
  Part1 = DHT22 Breakout module [package="Breakout board"]
  Componente2 = LCD1602-I2C
  Part2 = KY-018 Photoresistor Module [package="Breakout board"]
  Componente3 = Adafruit MiCS-5524 Gas Sensor [part_number="Adafruit #3199"]

nets:
  N1: Componente1.A0, Componente3.AOUT
  N2: Componente1.A1, Componente3.ENABLE
  N3: Componente1.A2, Part2.S
  N4: Componente1.A4/SDA, Componente2.SDA
  N5: Componente1.A5/SCL, Componente2.SCL
  N6: Componente1.D2, Part1.+
  5V: Componente1.5V, Part1.Out, Componente2.VCC, Part2.Vin, Componente3.5.0V
  GND: Componente1.GND, Part1.-, Componente2.GND, Part2.-, Componente3.GND

custom parts:
  DHT22 Breakout module: DHT22 temperature and humidity sensor module, provides a low-latency serial interface to measure humidity and temperature.
  LCD1602-I2C: A standard character display, usually with 2x16 characters. Comes in many colors with LCM1602 IIC attached.
  KY-018 Photoresistor Module: KY-018 Photoresistor module, used to measure light intensity. It can determine the presence or absence of light.
  Adafruit MiCS-5524 Gas Sensor: Give your next sensor project a nose for gasses with the Adafruit MiCS-5524 Gas Sensor Breakout. This breakout makes it easy to use this nice sensor from SGX Sensortech. The MiCS-5524 is a robust MEMS sensor for indoor carbon monoxide and natural gas leakage detection, it's suitable also for indoor air quality monitoring; breath checker and early fire detection. Please note: This sensor is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
