# Fritzing sketch RFid (saved by Fritzing 0.9.3b)

parts:
  Componente2 = Arduino Uno (Rev3)
  Componente3 = RFID-RC522-v3

nets:
  N1: Componente2.D9_PWM, Componente3.RST
  N2: Componente2.D10_PWM/SS, Componente3.SDA
  N3: Componente2.D11_PWM/MOSI, Componente3.MOSI
  N4: Componente2.D12/MISO, Componente3.MISO
  N5: Componente2.D13/SCK, Componente3.SCK
  3V3: Componente2.3V3, Componente3.3.3V
  GND: Componente2.GND, Componente3.GND

notes:
  Sda - 10
  Sck - 13
  Mosi - 11
  Miso - 12
  GND - GND
  Rst - 9
  3.3V - 3.3V

custom parts:
  RFID-RC522-v3: A simple China made RFID-RC522 Reader (6x4 cm); do check the pin labels, as this is a MFRC522 based clone.
