# Fritzing sketch Riego_v0 (saved by Fritzing 0.9.4)
breadboards: 1

parts:
  Componente1 = Arduino Uno (Rev3)
  KY-1 = Keyes Relay [package=THT]
  M1 = DC Motor
  JACK1 = 2.1mm Barrel Jack with Terminal Block

nets:
  N1: Componente1.D8, KY-1.signal
  N2: Componente1.5V, KY-1.power
  N3: Componente1.GND, KY-1.ground
  N4: KY-1.C, JACK1.POS
  N5: KY-1.NO, M1.pin_2
  N6: M1.pin_1, JACK1.NEG

custom parts:
  Keyes Relay: The Keyes 5V relay module is suitable for SCM development, home appliance control. It uses a 5V~12V TIL control signal which can control DC / AC signal.
