# Fritzing sketch Riego_v2 (saved by Fritzing 0.9.4)
breadboards: 1

parts:
  Componente1 = Arduino Uno (Rev3)
  KY-1 = Keyes Relay [package=THT]
  M1 = DC Motor
  JACK1 = 2.1mm Barrel Jack with Terminal Block
  Componente2 = FC-28 Soil Hygrometer Module - Probe
  Componente3 = FC-28 Soil Hygrometer Module

nets:
  N1: Componente1.A0, Componente3.AO
  N2: Componente1.D8, KY-1.signal
  5V: Componente1.5V, KY-1.power, Componente3.VCC
  GND: Componente1.GND, KY-1.ground, Componente3.GND
  N3: KY-1.C, JACK1.POS
  N4: KY-1.NO, M1.pin_2
  N5: M1.pin_1, JACK1.NEG
  N6: Componente2.POS, Componente3.POS
  N7: Componente2.NEG, Componente3.NEG

custom parts:
  Keyes Relay: The Keyes 5V relay module is suitable for SCM development, home appliance control. It uses a 5V~12V TIL control signal which can control DC / AC signal.
  FC-28 Soil Hygrometer Module - Probe: The FC-28 is a soil hygrometer module that uses the Texas Instruments LM393 comparator chip to provide an analog measurement of soil humidity.
  FC-28 Soil Hygrometer Module: The FC-28 is a soil hygrometer module that uses the Texas Instruments LM393 comparator chip to provide an analog measurement of soil humidity. The digital output is high when soil moisture is over a certain threshold, as determined by adjusting the potentiometer.
