# Fritzing sketch ServoMega (saved by Fritzing 0.9.4)

parts:
  Componente1 = Arduino Mega 2560 (Rev3)
  J1 = Basic Servo

nets:
  5V: Componente1.5V, J1.vcc
  GND: Componente1.GND, J1.gnd
  N1: Componente1.D2_PWM, J1.pulse
