# Fritzing sketch ServoPotMega (saved by Fritzing 0.9.4)
breadboards: 1

parts:
  R1 = Rotary Potentiometer (Small) [maximum_resistance=100kΩ package=THT]
  J1 = Basic Servo
  Componente2 = Arduino Mega 2560 (Rev3)

nets:
  GND: R1.leg1, J1.gnd, Componente2.GND
  N1: R1.wiper, Componente2.A0
  N2: R1.leg2, Componente2.5V
  N3: J1.pulse, Componente2.D9_PWM
