# Fritzing sketch Wifi_ESP8266 (saved by Fritzing 0.9.3b)
breadboards: 1

parts:
  U1 = ESP8266 WiFi Module [part_number=ESP8266]
  Componente1 = Arduino Uno (Rev3)
  C1 = Electrolytic Capacitor [capacitance=10μF package="0605 [SMD, electrolytic]"]
  R1 = Resistor [tolerance=±5% resistance=1k package=THT]
  R2 = Resistor [tolerance=±5% resistance=2.2k package=THT]

nets:
  N1: U1.RXD, R1.Pin_1, R2.Pin_0
  VCC: U1.VCC, U1.CH_PD, Componente1.3V3, C1.+
  GND: U1.GND, Componente1.GND, C1.-, R2.Pin_1
  N2: U1.TXD, Componente1.D6_PWM
  N3: Componente1.D7, R1.Pin_0

custom parts:
  ESP8266 WiFi Module: Generic WiFi Module based on the ESP8266 with onboard PCB antenna and UART communications
