# Fritzing sketch KeyoadLCDMega (saved by Fritzing 0.9.4)
breadboards: 1

parts:
  Componente3 = Arduino Mega 2560 (Rev3)
  Componente4 = LCD1602-I2C
  KEYPAD1 = Membrane Matrix Keypad  # not connected

nets:
  N1: Componente3.D21/SCL, Componente4.SCL
  N2: Componente3.D20/SDA, Componente4.SDA
  5V: Componente3.5V, Componente4.VCC
  GND: Componente3.GND, Componente4.GND

custom parts:
  LCD1602-I2C: A standard character display, usually with 2x16 characters. Comes in many colors with LCM1602 IIC attached.
  Membrane Matrix Keypad: Membrane Matrix 3x4 Keypad
